# Fritzing sketch Schaltplan (saved by Fritzing 0.9.3b)
breadboards: 1

parts:
  Bauteil1 = Arduino Uno (Rev3) - ICSP
  Bauteil2 = Bluetooth HC-05 Macho
  LED1 = LED - 3mm [color="Green (570nm)" package="3 mm [THT]"]  # not connected
  LED2 = LED - 3mm [color="White (4500K)" package="3 mm [THT]"]  # not connected
  LED3 = LED - 3mm [color="Blue (470nm)" package="3 mm [THT]"]  # not connected
  LED4 = LED - 3mm [color="Yellow (595nm)" package="3 mm [THT]"]  # not connected

nets:
  N1: Bauteil1.D2, Bauteil2.TXD
  N2: Bauteil1.D3_PWM, Bauteil2.RXD
  5V: Bauteil1.5V, Bauteil2.VCC
  GND: Bauteil1.GND, Bauteil2.GND
